# Fritzing sketch Untitled Sketch (saved by Fritzing 0.9.3b)

parts:
  Part1 = Adafruit Feather nRF52 [part_number="Adafruit #3406"]
  Part2 = Adafruit OLED FeatherWing [part_number="Adafruit #2900"]
  U4 = POT [package=alps_pot]
  U6 = POT [package=alps_pot]
  U7 = POT [package=alps_pot]
  U5 = POT [package=alps_pot]
  U8 = POT [package=alps_pot]
  U9 = POT [package=alps_pot]
  U10 = POT [package=alps_pot]
  U11 = POT [package=alps_pot]

nets:
  3.3V: Part1.3.3V, Part2.3.3V, U4.A, U6.A, U7.A, U5.A, U8.A, U9.A, U10.A, U11.A
  GND: Part1.GND, Part2.GND, U4.E, U6.E, U7.E, U5.E, U8.E, U9.E, U10.E, U11.E
  N1: Part1.A0/0.02, U4.S
  N2: Part1.A1/0.03, U5.S
  N3: Part1.A2/0.04, U6.S
  N4: Part1.A3/0.05, U7.S
  N5: Part1.A4/0.28, U8.S
  N6: Part1.A5/0.29, U11.S
  N7: Part1.SDA, Part2.SDA
  N8: Part1.SCL, Part2.SCL
  N9: Part1.A6/P0.30, U9.S
  N10: Part1.A7/P0.31, U10.S

custom parts:
  Adafruit OLED FeatherWing: This is the FeatherWing OLED: it adds a 128x32 monochrome OLED plus 3 user buttons to any Feather main board. These displays are small, only about 1" diagonal, but very readable due to the high contrast of an OLED display. This screen is made of 128x32 individual white OLED pixels and because the display makes its own light, no backlight is required. This reduces the power required to run the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
